# Fritzing sketch 01 Blink LED (saved by Fritzing 0.9.4)
breadboards: 1

parts:
  Мигающий_светодиод = Arduino Uno (Rev3)
  LED1 = LED - 5mm [color="Red (633nm)" package="5 mm [THT]"]
  R1 = Resistor [tolerance=±5% resistance=220 package=THT]

nets:
  N1: Мигающий_светодиод.D9_PWM, R1.Pin_1
  N2: Мигающий_светодиод.GND, LED1.cathode
  N3: LED1.anode, R1.Pin_0
