# Fritzing sketch 02a LED Flowing Lights (saved by Fritzing 0.9.4)
breadboards: 1

parts:
  R1 = Resistor [tolerance=±5% resistance=220 package=THT]
  R2 = Resistor [tolerance=±5% resistance=220 package=THT]
  R3 = Resistor [tolerance=±5% resistance=220 package=THT]
  R4 = Resistor [tolerance=±5% resistance=220 package=THT]
  R5 = Resistor [tolerance=±5% resistance=220 package=THT]
  R6 = Resistor [tolerance=±5% resistance=220 package=THT]
  LED1 = LED - 5mm [color="Red (633nm)" package="5 mm [THT]"]
  LED2 = LED - 5mm [color="Green (570nm)" package="5 mm [THT]"]
  LED3 = LED - 5mm [color="Yellow (595nm)" package="5 mm [THT]"]
  LED4 = LED - 5mm [color="Red (633nm)" package="5 mm [THT]"]
  LED5 = LED - 5mm [color="Green (570nm)" package="5 mm [THT]"]
  LED6 = LED - 5mm [color="Yellow (595nm)" package="5 mm [THT]"]
  LED7 = LED - 5mm [color="Red (633nm)" package="5 mm [THT]"]
  LED8 = LED - 5mm [color="Red (633nm)" package="5 mm [THT]"]
  R7 = Resistor [tolerance=±5% resistance=220 package=THT]
  R8 = Resistor [tolerance=±5% resistance=220 package=THT]
  元件1 = Arduino Uno (Rev3) - ICSP

nets:
  N1: R1.Pin_0, LED1.anode
  N2: R1.Pin_1, 元件1.D2
  N3: R2.Pin_0, 元件1.D3_PWM
  N4: R2.Pin_1, LED2.anode
  N5: R3.Pin_0, 元件1.D4
  N6: R3.Pin_1, LED3.anode
  N7: R4.Pin_0, 元件1.D5_PWM
  N8: R4.Pin_1, LED4.anode
  N9: R5.Pin_0, 元件1.D7
  N10: R5.Pin_1, LED6.anode
  N11: R6.Pin_0, 元件1.D6_PWM
  N12: R6.Pin_1, LED5.anode
  N13: LED1.cathode, LED2.cathode, LED3.cathode, LED4.cathode, LED5.cathode, LED6.cathode, LED7.cathode, LED8.cathode, 元件1.GND
  N14: LED7.anode, R7.Pin_1
  N15: LED8.anode, R8.Pin_1
  N16: R7.Pin_0, 元件1.D8
  N17: R8.Pin_0, 元件1.D9_PWM

// code stored in the sketch: 02a LED Flowing Lights.ino
//Flowing LED Lights
/* Eight LEDs will light up one by one from left to right, and then go out one by one from right to left.
After that, the LEDs will light up one by one from right to left, and then go out one by one from left to right.
This process will repeat indefinitely.*/
//www.RobotLinking.com
//2015.5.7
/**************************************/
const int lowestPin = 2;//the lowest one attach to
const int highestPin = 9;//the highest one attach to 
/**************************************/
void setup()
{
  //set pins 1 through 6 as output  
  for(int thisPin = lowestPin;thisPin <= highestPin;thisPin++)
  {
     pinMode(thisPin,OUTPUT); //initialize thisPin as an output
  }
} 
/****************************************/
void loop()
{
  //iterate over the pins
  //turn the led on from lowest to the highest
  for(int thisPin = lowestPin;thisPin <= highestPin;thisPin++)
  {
    digitalWrite(thisPin,HIGH);//turn this led on
    delay(100);//wait for 100 microseconds
  }
  //fade from the highest to the lowest
  for(int thisPin = highestPin;thisPin>=lowestPin;thisPin--)
  {
    digitalWrite(thisPin,LOW);//turn this led off
    delay(100);//wait for 100 microseconds
  }
  for(int thisPin = highestPin;thisPin>=lowestPin;thisPin--)
  {
    digitalWrite(thisPin,HIGH);//turn this led off
    delay(100);//wait for 100 microseconds
  }
  for(int thisPin = lowestPin;thisPin <= highestPin;thisPin++)
  {
    digitalWrite(thisPin,LOW);//turn this led on
    delay(100);//wait for 100 microseconds
  }
}
